# Fritzing sketch Schema (saved by Fritzing 0.9.3b)
circuit board: 10.1634cm x 7.69285cm
breadboards: 1

parts:
  Part1 = Arduino Uno (Rev3)
  DPDT_Relay1 = DPDT Relay [chip_label=Relay package="DIP (Dual Inline) [THT]"]
  Q1 = TRANSISTOR_NPN [package=to-92]
  R1 = Resistor [tolerance=±5% resistance=4.7k package=THT]
  DPDT_Relay2 = DPDT Relay [chip_label=Relay package="DIP (Dual Inline) [THT]"]
  Q2 = TRANSISTOR_NPN [package=to-92]
  R2 = Resistor [tolerance=±5% resistance=4.7k package=THT]
  R4 = Resistor [tolerance=±5% resistance=220 package=THT]
  R5 = Resistor [tolerance=±5% resistance=1k package=THT]
  R6 = Resistor [tolerance=±5% resistance=1k package=THT]
  R7 = Resistor [tolerance=±5% resistance=1k package=THT]
  R8 = Resistor [tolerance=±5% resistance=1k package=THT]
  R9 = Resistor [tolerance=±5% resistance=10k package=THT]
  R10 = Resistor [tolerance=±5% resistance=10k package=THT]
  R11 = Resistor [tolerance=±5% resistance=10k package=THT]
  R12 = Resistor [tolerance=±5% resistance=10k package=THT]
  R13 = Resistor [tolerance=±5% resistance=10k package=THT]
  R14 = Resistor [tolerance=±5% resistance=10k package=THT]
  Out = Header 3 [package=jst-3-pth]
  LEFT = Header 3 [package=jst-3-pth]
  RIGHT = Header 3 [package=jst-3-pth]
  POTENC = Header 3 [package=jst-3-pth]
  VOL_SWITCH = Header 2 [package=jst-2-smd]
  ROT_SWITCH = Header 5 [package=1x05-1mm-ra]
  LEDTX2 = Header 2 [package=jst-2-smd]
  LEDTX1 = Header 2 [package=jst-2-smd]
  LEDRX2 = Header 2 [package=jst-2-smd]
  LEDRX1 = Header 2 [package=jst-2-smd]
  KEYOUT2 = Header 2 [package=jst-2-smd]
  KEYOUT1 = Header 2 [package=jst-2-smd]
  D3 = Rectifier Diode [part_number=1N4001 package="Melf DO-213 AB [SMD]"]
  D2 = Rectifier Diode [part_number=1N4001 package="Melf DO-213 AB [SMD]"]

nets:
  N1: Part1.D8, R5.Pin_0
  N2: Part1.D9_PWM, R6.Pin_0
  N3: Part1.D10_PWM/SS, R7.Pin_0
  N4: Part1.D11_PWM/MOSI, R8.Pin_0
  N5: Part1.D13/SCK, R2.Pin_1
  N6: Part1.GND, Q1.E, Q2.E, Out.3, LEFT.3, RIGHT.3, ROT_SWITCH.5, LEDTX2.2, LEDTX1.2, LEDRX2.2, LEDRX1.2, KEYOUT2.2, KEYOUT1.2
  N7: Part1.D2, R1.Pin_1
  N8: Part1.D3_PWM, R14.Pin_1, KEYOUT1.1
  N9: Part1.D5_PWM, R13.Pin_1, KEYOUT2.1
  N10: Part1.5V, DPDT_Relay2.pin8, R9.Pin_1, R10.Pin_1, R11.Pin_1, R12.Pin_1, R13.Pin_0, R14.Pin_0, D3.cathode
  N11: DPDT_Relay1.pin1, D2.cathode
  N12: DPDT_Relay1.pin2, LEFT.1
  N13: DPDT_Relay1.pin3, R4.Pin_1, Out.1
  N14: DPDT_Relay1.pin4, RIGHT.1
  N15: DPDT_Relay1.pin5, DPDT_Relay2.pin4, RIGHT.2
  N16: DPDT_Relay1.pin6, DPDT_Relay2.pin2
  N17: DPDT_Relay1.pin7, LEFT.2
  N18: DPDT_Relay1.pin8, Q1.C, D2.anode
  N19: Q1.B, R1.Pin_0
  N20: DPDT_Relay2.pin1, Q2.C, D3.anode
  N21: DPDT_Relay2.pin3, DPDT_Relay2.pin6, Out.2
  N22: DPDT_Relay2.pin5, VOL_SWITCH.2
  N23: Q2.B, R2.Pin_0
  N24: R4.Pin_0, POTENC.1, POTENC.2
  N25: R5.Pin_1, LEDRX1.1
  N26: R6.Pin_1, LEDRX2.1
  N27: R7.Pin_1, LEDTX1.1
  N28: R8.Pin_1, LEDTX2.1
  N29: R9.Pin_0, ROT_SWITCH.2
  N30: R10.Pin_0, ROT_SWITCH.3
  N31: R11.Pin_0, ROT_SWITCH.1
  N32: R12.Pin_0, ROT_SWITCH.4
  N33: POTENC.3, VOL_SWITCH.1

custom parts:
  DPDT Relay: DIP DPDT Relay (Double Pole Double Throw)
